# Fritzing sketch rangkaian (saved by Fritzing 0.9.3b)

parts:
  Load_Cell1 = Load Cell - Red/white/black/green
  Part1 = HX711 Weighing Sensor Module
  U1 = ESP32-38PinWide [part_number=ESP32-38PinWide]
  LCM1602_IIC1 = LCM1602 IIC [part_number="LCM1602 IIC" chip_label="LCM1602 IIC" package="DIP (Dual Inline) [THT]"]
  LCD1 = LCD screen
  hc-sr1 = hc-sr04
  hc-sr2 = hc-sr04

nets:
  N1: Load_Cell1.wire1, Part1.E+
  N2: Load_Cell1.wire2, Part1.A+
  N3: Load_Cell1.wire3, Part1.E-
  N4: Load_Cell1.wire4, Part1.A-
  VCC: Part1.VCC, U1.VIN, LCM1602_IIC1.VCC, hc-sr1.VCC, hc-sr2.VCC
  GND: Part1.GND, U1.GND, LCM1602_IIC1.GND
  N5: Part1.DO/RX, U1.GPIO18
  N6: Part1.CK/TX, U1.GPIO19
  N7: U1.GPIO25, hc-sr1.Trig
  N8: U1.GPIO26, hc-sr1.Echo
  GND_2: U1.GPIO11, hc-sr1.GND, hc-sr2.GND
  N9: U1.GPIO16, hc-sr2.Echo
  N10: U1.GPIO17, hc-sr2.Trig
  N11: U1.GPIO21, LCM1602_IIC1.SDA
  N12: U1.GPIO22, LCM1602_IIC1.SCL
  VSS: LCM1602_IIC1.VSS, LCD1.VSS
  VDD: LCM1602_IIC1.VDD, LCD1.VDD
  N13: LCM1602_IIC1.V0, LCD1.V0
  N14: LCM1602_IIC1.RS, LCD1.RS
  N15: LCM1602_IIC1.RW, LCD1.R/W
  N16: LCM1602_IIC1.E, LCD1.E
  N17: LCM1602_IIC1.D0, LCD1.DB0
  N18: LCM1602_IIC1.D1, LCD1.DB1
  N19: LCM1602_IIC1.D2, LCD1.DB2
  N20: LCM1602_IIC1.D3, LCD1.DB3
  N21: LCM1602_IIC1.D4, LCD1.DB4
  N22: LCM1602_IIC1.D5, LCD1.DB5
  N23: LCM1602_IIC1.D6, LCD1.DB6
  N24: LCM1602_IIC1.D7, LCD1.DB7
  N25: LCM1602_IIC1.A, LCD1.LED+
  N26: LCM1602_IIC1.K, LCD1.LED-

custom parts:
  Load Cell - Red/white/black/green: A rectangle load cell/weighting pressure Sensor with four wires - Red, white, black, green. Normally corresponding with E+, E-, A+, A- respectively.
  HX711 Weighing Sensor Module: HX711 is a precision 24-bit analog-to-digital converter (ADC) designed for weigh scales and industrial control applications to interface directly with a bridge sensor.
  ESP32-38PinWide: Generic 38-Pin ESP32 with wide format (only access to one side of pins on a breadboard) based on Stephen Lilley's HiLetgo ESP-WROOM-32 ESP32 ESP-32S Development Board.
  LCM1602 IIC: I2C-Module to use a 1602 or 2004 LCD on with the wire.h libory Serial LCD Modul
